// Logisim project EP02.circ as structural Verilog: 7 circuits, main circuit main
module HalfSum (
  input  in_1,
  input  in_2,
  output out_3,
  output out_4
);

  wire not_1_out, or_1_out;

  or or_1 (or_1_out, in_1, in_2);
  and and_1 (out_4, in_2, in_1);
  and and_2 (out_3, or_1_out, not_1_out);
  not not_1 (not_1_out, out_4);
endmodule

module FullSum (
  input  in_1,
  input  in_2,
  input  in_3,
  output out_4,
  output out_5
);

  wire halfsum_1_out_3, halfsum_1_out_4, halfsum_2_out_4;

  HalfSum halfsum_1 (.in_1(in_3), .in_2(in_2), .out_3(halfsum_1_out_3), .out_4(halfsum_1_out_4));
  HalfSum halfsum_2 (.in_1(halfsum_1_out_3), .in_2(in_1), .out_3(out_4), .out_4(halfsum_2_out_4));
  or or_1 (out_5, halfsum_2_out_4, halfsum_1_out_4);
endmodule

module Mux2 (
  input  a0,
  input  b0,
  input  c0,
  input  d0,
  input  op1,
  input  op0,
  output s
);

  wire and_1_out, and_2_out, and_3_out, and_4_out, not_1_out, not_2_out, not_3_out, not_4_out;

  not not_1 (not_1_out, op1);
  and and_1 (and_1_out, a0, not_1_out, not_2_out);
  not not_2 (not_2_out, op0);
  not not_3 (not_3_out, op1);
  and and_2 (and_2_out, b0, not_3_out, op0);
  and and_3 (and_3_out, c0, op1, not_4_out);
  not not_4 (not_4_out, op0);
  and and_4 (and_4_out, d0, op1, op0);
  or or_1 (s, and_1_out, and_2_out, and_3_out, and_4_out);
endmodule

module Mux1 (
  input  in_1,
  input  in_2,
  input  in_3,
  output out_4
);

  wire and_1_out, and_2_out, not_1_out;

  and and_1 (and_1_out, in_1, not_1_out);
  not not_1 (not_1_out, in_3);
  and and_2 (and_2_out, in_2, in_3);
  or or_1 (out_4, and_1_out, and_2_out);
endmodule

module ULA (
  input  a,
  input  b,
  input  Cin,
  input  InvB,
  input  in_5,
  input  in_6,
  output s,
  output Overflow
);

  wire and_1_out, fullsum_1_out_4, mux1_1_out_4, not_1_out, not_2_out, or_1_out, or_2_out;

  or or_1 (or_1_out, Cin, InvB);
  Mux1 mux1_1 (.in_1(b), .in_2(not_1_out), .in_3(InvB), .out_4(mux1_1_out_4));
  not not_1 (not_1_out, b);
  and and_1 (and_1_out, a, b);
  or or_2 (or_2_out, a, b);
  not not_2 (not_2_out, a);
  FullSum fullsum_1 (.out_4(fullsum_1_out_4), .out_5(Overflow), .in_1(or_1_out), .in_2(a), .in_3(mux1_1_out_4));
  Mux2 mux2_1 (.a0(and_1_out), .b0(or_2_out), .c0(not_2_out), .d0(fullsum_1_out_4), .s(s), .op1(in_5), .op0(in_6));
endmodule

module ULA4 (
  input  Cin,
  input  InvB,
  input  A0,
  input  B0,
  input  A1,
  input  B1,
  input  A2,
  input  B2,
  input  A3,
  input  B3,
  input  OP1,
  input  OP0,
  output s0,
  output s1,
  output s2,
  output s3,
  output Overflow
);

  wire ula_1_overflow, ula_2_overflow, ula_3_overflow;

  ULA ula_1 (.a(A0), .b(B0), .InvB(InvB), .s(s0), .Overflow(ula_1_overflow), .in_5(OP1), .in_6(OP0), .Cin(Cin));
  ULA ula_2 (
    .a(A1), .b(B1), .InvB(InvB), .s(s1), .Overflow(ula_2_overflow), .in_5(OP1), .in_6(OP0),
    .Cin(ula_1_overflow));
  ULA ula_3 (
    .a(A2), .b(B2), .InvB(InvB), .s(s2), .Overflow(ula_3_overflow), .in_5(OP1), .in_6(OP0),
    .Cin(ula_2_overflow));
  ULA ula_4 (.a(A3), .b(B3), .InvB(InvB), .s(s3), .Overflow(Overflow), .in_5(OP1), .in_6(OP0), .Cin(ula_3_overflow));
endmodule

module main (
);

  ULA4 ula4_1 ();  // open: Cin, InvB, A0, B0, A1, B1, A2, B2, A3, B3, OP1, OP0, Overflow, s0, s1, s2, s3
endmodule
