// Logisim project EP01.circ as structural Verilog: 8 circuits, main circuit half-sum
module half_sum (
  input  in_1,
  input  in_2,
  output out_3,
  output out_4
);

  wire not_1_out, or_1_out;

  or or_1 (or_1_out, in_2, in_1);
  and and_1 (out_4, in_1, in_2);
  and and_2 (out_3, or_1_out, not_1_out);
  not not_1 (not_1_out, out_4);
endmodule

module Full_Sum (
  input  in_1,
  input  in_2,
  input  in_3,
  output out_4,
  output out_5
);

  wire half_sum_1_out_4, half_sum_2_out_3, half_sum_2_out_4;

  half_sum half_sum_1 (.in_1(half_sum_2_out_3), .in_2(in_3), .out_3(out_4), .out_4(half_sum_1_out_4));
  half_sum half_sum_2 (.in_1(in_1), .in_2(in_2), .out_3(half_sum_2_out_3), .out_4(half_sum_2_out_4));
  or or_1 (out_5, half_sum_1_out_4, half_sum_2_out_4);
endmodule

module Full_Sum_B (
  input  Cin,
  input  A,
  input  B,
  output s,
  output Cout
);

  wire and_1_out, and_2_out, xor_1_out;

  xor xor_1 (xor_1_out, A, B);
  and and_1 (and_1_out, Cin, xor_1_out);
  and and_2 (and_2_out, B, A);
  xor xor_2 (s, Cin, xor_1_out);
  or or_1 (Cout, and_1_out, and_2_out);

  // Notes on the sheet:
  //   10ns
  //   10ns
  //   20ns
  //   20ns
  //   30ns
endmodule

module _4B_Sum (
  input  Cin,
  input  x0,
  input  y0,
  input  x1,
  input  y1,
  input  x2,
  input  y2,
  input  x3,
  input  y3,
  output s0,
  output s1,
  output s2,
  output s3,
  output Cout,
  output Overflow
);

  wire full_sum_1_out_5, full_sum_2_out_5, full_sum_3_out_5;

  Full_Sum full_sum_1 (.in_1(y0), .in_2(x0), .in_3(Cin), .out_4(s0), .out_5(full_sum_1_out_5));
  Full_Sum full_sum_2 (.in_1(y1), .in_2(x1), .in_3(full_sum_1_out_5), .out_4(s1), .out_5(full_sum_2_out_5));
  Full_Sum full_sum_3 (.in_1(y2), .in_2(x2), .in_3(full_sum_2_out_5), .out_4(s2), .out_5(full_sum_3_out_5));
  Full_Sum full_sum_4 (.in_1(y3), .in_2(x3), .in_3(full_sum_3_out_5), .out_4(s3), .out_5(Cout));
  xor xor_1 (Overflow, Cout, full_sum_3_out_5);
endmodule

module _4B_sumb (
  input  in_1,
  input  [3:0] in_2,
  input  [3:0] in_3,
  output [3:0] out_4,
  output out_5
);

  _4B_Sum u_4b_sum_1 (
    .x0(in_2[0]), .y0(in_3[0]), .x1(in_2[1]), .y1(in_3[1]), .x2(in_2[2]), .y2(in_3[2]), .x3(in_2[3]),
    .y3(in_3[3]), .s0(out_4[3]), .s1(out_4[2]), .s2(out_4[1]), .s3(out_4[0]), .Cout(out_5), .Cin(in_1));  // open: Overflow
endmodule

module Decoder (
  input  e3,
  input  e2,
  input  e1,
  input  e0,
  output a,
  output b,
  output c,
  output d,
  output e,
  output f,
  output g
);

  wire and_1_out, and_2_out, and_3_out, and_4_out, and_5_out, and_6_out, and_7_out, and_8_out, and_9_out,
       and_10_out, and_11_out, and_12_out, and_13_out, and_14_out, and_15_out, and_16_out, and_17_out,
       and_18_out, and_19_out, and_20_out, and_21_out, and_22_out, and_23_out, and_24_out, and_25_out,
       and_26_out, and_27_out, and_28_out, and_29_out, and_30_out, and_31_out, and_32_out, and_33_out,
       and_34_out, and_35_out, not_1_out, not_2_out, not_3_out, not_4_out, not_5_out, not_6_out, not_7_out,
       not_8_out, not_9_out, not_10_out, not_11_out, not_12_out, not_13_out, not_14_out, not_15_out,
       not_16_out, not_17_out, not_18_out, not_19_out, not_20_out, not_21_out, not_22_out, not_23_out,
       not_24_out, not_25_out, not_26_out, not_27_out, not_28_out, not_29_out, not_30_out, not_31_out,
       not_32_out, not_33_out, not_34_out, not_35_out, not_36_out, not_37_out, not_38_out, not_39_out,
       not_40_out, not_41_out, not_42_out, not_43_out;

  not not_1 (not_1_out, e2);
  and and_1 (and_1_out, not_1_out, not_2_out);
  not not_2 (not_2_out, e0);
  not not_3 (not_3_out, e3);
  and and_2 (and_2_out, not_3_out, e1);
  not not_4 (not_4_out, e3);
  and and_3 (and_3_out, not_4_out, e2, e0);
  and and_4 (and_4_out, e2, e1);
  not not_5 (not_5_out, e2);
  and and_5 (and_5_out, e3, not_5_out, not_6_out);
  not not_6 (not_6_out, e1);
  and and_6 (and_6_out, e3, not_7_out);
  not not_7 (not_7_out, e0);
  not not_8 (not_8_out, e3);
  and and_7 (and_7_out, not_8_out, not_9_out);
  not not_9 (not_9_out, e2);
  not not_10 (not_10_out, e3);
  not not_11 (not_11_out, e1);
  and and_8 (and_8_out, not_10_out, not_11_out, not_12_out);
  not not_12 (not_12_out, e0);
  not not_13 (not_13_out, e2);
  and and_9 (and_9_out, not_13_out, not_14_out);
  not not_14 (not_14_out, e0);
  not not_15 (not_15_out, e3);
  and and_10 (and_10_out, not_15_out, e1, e0);
  not not_16 (not_16_out, e1);
  and and_11 (and_11_out, e3, not_16_out, e0);
  not not_17 (not_17_out, e3);
  and and_12 (and_12_out, not_17_out, not_18_out);
  not not_18 (not_18_out, e1);
  not not_19 (not_19_out, e3);
  and and_13 (and_13_out, not_19_out, e0);
  not not_20 (not_20_out, e1);
  and and_14 (and_14_out, not_20_out, e0);
  not not_21 (not_21_out, e3);
  and and_15 (and_15_out, not_21_out, e2);
  and and_16 (and_16_out, e3, not_22_out);
  not not_22 (not_22_out, e2);
  not not_23 (not_23_out, e3);
  not not_24 (not_24_out, e2);
  and and_17 (and_17_out, not_23_out, not_24_out, not_25_out);
  not not_25 (not_25_out, e0);
  not not_26 (not_26_out, e2);
  and and_18 (and_18_out, not_26_out, e1, e0);
  not not_27 (not_27_out, e1);
  and and_19 (and_19_out, e2, not_27_out, e0);
  and and_20 (and_20_out, e2, e1, not_28_out);
  not not_28 (not_28_out, e0);
  and and_21 (and_21_out, e3, not_29_out);
  not not_29 (not_29_out, e1);
  not not_30 (not_30_out, e2);
  and and_22 (and_22_out, not_30_out, not_31_out);
  not not_31 (not_31_out, e0);
  and and_23 (and_23_out, e1, not_32_out);
  not not_32 (not_32_out, e0);
  and and_24 (and_24_out, e3, e1);
  and and_25 (and_25_out, e3, e2);
  not not_33 (not_33_out, e1);
  and and_26 (and_26_out, not_33_out, not_34_out);
  not not_34 (not_34_out, e0);
  not not_35 (not_35_out, e3);
  and and_27 (and_27_out, not_35_out, e2, not_36_out);
  not not_36 (not_36_out, e1);
  and and_28 (and_28_out, e2, not_37_out);
  not not_37 (not_37_out, e0);
  and and_29 (and_29_out, e3, not_38_out);
  not not_38 (not_38_out, e2);
  and and_30 (and_30_out, e3, e1);
  not not_39 (not_39_out, e2);
  and and_31 (and_31_out, not_39_out, e1);
  and and_32 (and_32_out, e1, not_40_out);
  not not_40 (not_40_out, e0);
  not not_41 (not_41_out, e3);
  and and_33 (and_33_out, not_41_out, e2, not_42_out);
  not not_42 (not_42_out, e1);
  and and_34 (and_34_out, e3, not_43_out);
  not not_43 (not_43_out, e2);
  and and_35 (and_35_out, e3, e0);
  or or_1 (b, and_7_out, and_8_out, and_9_out, and_10_out, and_11_out);
  or or_2 (c, and_12_out, and_13_out, and_14_out, and_15_out, and_16_out);
  or or_3 (d, and_17_out, and_18_out, and_19_out, and_20_out, and_21_out);
  or or_4 (e, and_22_out, and_23_out, and_24_out, and_25_out);
  or or_5 (f, and_26_out, and_27_out, and_28_out, and_29_out, and_30_out);
  or or_6 (g, and_31_out, and_32_out, and_33_out, and_34_out, and_35_out);
  or or_7 (a, and_1_out, and_2_out, and_3_out, and_4_out, and_5_out, and_6_out);
endmodule

module main (
  input  in_1,
  input  [3:0] in_2,
  input  [3:0] in_3,
  output out_4
);

  wire decoder_1_a, decoder_1_b, decoder_1_c, decoder_1_d, decoder_1_e, decoder_1_f, decoder_1_g,
       decoder_2_a, decoder_2_b, decoder_2_c, decoder_2_d, decoder_2_e, decoder_2_f, decoder_2_g,
       decoder_3_a, decoder_3_b, decoder_3_c, decoder_3_d, decoder_3_e, decoder_3_f, decoder_3_g;
  wire [3:0] n4b_sumb_1_out_4;

  _4B_sumb u_4b_sumb_1 (.in_2(in_2), .in_3(in_3), .out_4(n4b_sumb_1_out_4), .out_5(out_4), .in_1(in_1));
  Decoder decoder_1 (
    .e3(in_2[3]), .e2(in_2[2]), .e1(in_2[1]), .a(decoder_1_a), .e0(in_2[0]), .b(decoder_1_b),
    .c(decoder_1_c), .d(decoder_1_d), .e(decoder_1_e), .f(decoder_1_f), .g(decoder_1_g));
  Decoder decoder_2 (
    .e3(in_3[3]), .e2(in_3[2]), .e1(in_3[1]), .a(decoder_2_a), .e0(in_3[0]), .b(decoder_2_b),
    .c(decoder_2_c), .d(decoder_2_d), .e(decoder_2_e), .f(decoder_2_f), .g(decoder_2_g));
  _7_Segment_Display u_7_segment_display_1 (
    .g(decoder_1_g), .f(decoder_1_f), .a(decoder_1_a), .b(decoder_1_b), .e(decoder_1_e), .d(decoder_1_d),
    .c(decoder_1_c));  // open: dp
  Decoder decoder_3 (
    .e3(n4b_sumb_1_out_4[3]), .e2(n4b_sumb_1_out_4[2]), .e1(n4b_sumb_1_out_4[1]), .a(decoder_3_a),
    .e0(n4b_sumb_1_out_4[0]), .b(decoder_3_b), .c(decoder_3_c), .d(decoder_3_d), .e(decoder_3_e),
    .f(decoder_3_f), .g(decoder_3_g));
  _7_Segment_Display u_7_segment_display_2 (
    .g(decoder_2_g), .f(decoder_2_f), .a(decoder_2_a), .b(decoder_2_b), .e(decoder_2_e), .d(decoder_2_d),
    .c(decoder_2_c));  // open: dp
  _7_Segment_Display u_7_segment_display_3 (
    .g(decoder_3_g), .f(decoder_3_f), .a(decoder_3_a), .b(decoder_3_b), .e(decoder_3_e), .d(decoder_3_d),
    .c(decoder_3_c));  // open: dp
endmodule

module main2 (
  input  X0,
  input  X1,
  input  X2,
  input  X3,
  input  Cin,
  input  Y0,
  input  Y1,
  input  Y2,
  input  Y3,
  output Overflow,
  output Cout
);

  wire decoder_1_a, decoder_1_b, decoder_1_c, decoder_1_d, decoder_1_e, decoder_1_f, decoder_1_g,
       decoder_2_a, decoder_2_b, decoder_2_c, decoder_2_d, decoder_2_e, decoder_2_f, decoder_2_g,
       decoder_3_a, decoder_3_b, decoder_3_c, decoder_3_d, decoder_3_e, decoder_3_f, decoder_3_g,
       n4b_sum_1_s0, n4b_sum_1_s1, n4b_sum_1_s2, n4b_sum_1_s3;

  Decoder decoder_1 (
    .e3(X3), .e2(X2), .e1(X1), .a(decoder_1_a), .e0(X0), .b(decoder_1_b), .c(decoder_1_c), .d(decoder_1_d),
    .e(decoder_1_e), .f(decoder_1_f), .g(decoder_1_g));
  _4B_Sum u_4b_sum_1 (
    .x0(X0), .y0(Y0), .x1(X1), .y1(Y1), .x2(X2), .y2(Y2), .x3(X3), .y3(Y3), .s0(n4b_sum_1_s0),
    .s1(n4b_sum_1_s1), .s2(n4b_sum_1_s2), .s3(n4b_sum_1_s3), .Cout(Cout), .Cin(Cin), .Overflow(Overflow));
  Decoder decoder_2 (
    .e3(Y3), .e2(Y2), .e1(Y1), .a(decoder_2_a), .e0(Y0), .b(decoder_2_b), .c(decoder_2_c), .d(decoder_2_d),
    .e(decoder_2_e), .f(decoder_2_f), .g(decoder_2_g));
  _7_Segment_Display u_7_segment_display_1 (
    .g(decoder_1_g), .f(decoder_1_f), .a(decoder_1_a), .b(decoder_1_b), .e(decoder_1_e), .d(decoder_1_d),
    .c(decoder_1_c));  // open: dp
  Decoder decoder_3 (
    .e3(n4b_sum_1_s3), .e2(n4b_sum_1_s2), .e1(n4b_sum_1_s1), .a(decoder_3_a), .e0(n4b_sum_1_s0),
    .b(decoder_3_b), .c(decoder_3_c), .d(decoder_3_d), .e(decoder_3_e), .f(decoder_3_f), .g(decoder_3_g));
  _7_Segment_Display u_7_segment_display_2 (
    .g(decoder_2_g), .f(decoder_2_f), .a(decoder_2_a), .b(decoder_2_b), .e(decoder_2_e), .d(decoder_2_d),
    .c(decoder_2_c));  // open: dp
  _7_Segment_Display u_7_segment_display_3 (
    .g(decoder_3_g), .f(decoder_3_f), .a(decoder_3_a), .b(decoder_3_b), .e(decoder_3_e), .d(decoder_3_d),
    .c(decoder_3_c));  // open: dp
endmodule
