// Logisim project EP02.circ as structural Verilog: 9 circuits, main circuit main
module HalfSum (
  input  in_1,
  input  in_2,
  output out_3,
  output out_4
);

  wire not_1_out, or_1_out;

  or or_1 (or_1_out, in_1, in_2);
  and and_1 (out_4, in_2, in_1);
  and and_2 (out_3, or_1_out, not_1_out);
  not not_1 (not_1_out, out_4);
endmodule

module FullSum (
  input  in_1,
  input  in_2,
  input  in_3,
  output out_4,
  output out_5
);

  wire halfsum_1_out_3, halfsum_1_out_4, halfsum_2_out_4;

  HalfSum halfsum_1 (.in_1(in_3), .in_2(in_2), .out_3(halfsum_1_out_3), .out_4(halfsum_1_out_4));
  HalfSum halfsum_2 (.in_1(halfsum_1_out_3), .in_2(in_1), .out_3(out_4), .out_4(halfsum_2_out_4));
  or or_1 (out_5, halfsum_2_out_4, halfsum_1_out_4);
endmodule

module Mux1 (
  input  in_1,
  input  in_2,
  input  in_3,
  output out_4
);

  wire and_1_out, and_2_out, not_1_out;

  and and_1 (and_1_out, in_1, not_1_out);
  not not_1 (not_1_out, in_3);
  and and_2 (and_2_out, in_2, in_3);
  or or_1 (out_4, and_1_out, and_2_out);
endmodule

module Mux2 (
  input  a0,
  input  b0,
  input  c0,
  input  d0,
  input  op1,
  input  op0,
  output s
);

  wire and_1_out, and_2_out, and_3_out, and_4_out, not_1_out, not_2_out, not_3_out, not_4_out;

  and and_1 (and_1_out, a0, not_1_out, not_2_out);
  not not_1 (not_1_out, op1);
  not not_2 (not_2_out, op0);
  and and_2 (and_2_out, b0, not_3_out, op0);
  not not_3 (not_3_out, op1);
  and and_3 (and_3_out, c0, op1, not_4_out);
  not not_4 (not_4_out, op0);
  and and_4 (and_4_out, d0, op1, op0);
  or or_1 (s, and_1_out, and_2_out, and_3_out, and_4_out);
endmodule

module ULA1_1Bit (
  input  a,
  input  b,
  input  Cin,
  input  InvB,
  input  OP1,
  input  OP0,
  output s,
  output Overflow
);

  wire and_1_out, fullsum_1_out_4, mux1_1_out_4, not_1_out, not_2_out, or_1_out, or_2_out;

  or or_1 (or_1_out, Cin, InvB);
  Mux1 mux1_1 (.in_1(b), .in_2(not_1_out), .out_4(mux1_1_out_4), .in_3(InvB));
  not not_1 (not_1_out, b);
  and and_1 (and_1_out, a, b);
  or or_2 (or_2_out, a, b);
  not not_2 (not_2_out, a);
  FullSum fullsum_1 (.out_4(fullsum_1_out_4), .out_5(Overflow), .in_1(or_1_out), .in_2(a), .in_3(mux1_1_out_4));
  Mux2 mux2_1 (.a0(and_1_out), .b0(or_2_out), .c0(not_2_out), .d0(fullsum_1_out_4), .s(s), .op1(OP1), .op0(OP0));
endmodule

module ULA1_4Bits (
  input  InvB,
  input  Cin,
  input  B3,
  input  B2,
  input  B1,
  input  B0,
  input  A3,
  input  A2,
  input  A1,
  input  A0,
  input  OP1,
  input  OP0,
  output s0,
  output s1,
  output s2,
  output s3,
  output Overflow
);

  wire ula1_1bit_1_overflow, ula1_1bit_2_overflow, ula1_1bit_3_overflow;

  ULA1_1Bit ula1_1bit_1 (
    .a(A0), .b(B0), .InvB(InvB), .s(s0), .Overflow(ula1_1bit_1_overflow), .OP1(OP1), .OP0(OP0), .Cin(Cin));
  ULA1_1Bit ula1_1bit_2 (
    .a(A1), .b(B1), .InvB(InvB), .s(s1), .Overflow(ula1_1bit_2_overflow), .OP1(OP1), .OP0(OP0),
    .Cin(ula1_1bit_1_overflow));
  ULA1_1Bit ula1_1bit_3 (
    .a(A2), .b(B2), .InvB(InvB), .s(s2), .Overflow(ula1_1bit_3_overflow), .OP1(OP1), .OP0(OP0),
    .Cin(ula1_1bit_2_overflow));
  ULA1_1Bit ula1_1bit_4 (
    .a(A3), .b(B3), .InvB(InvB), .s(s3), .Overflow(Overflow), .OP1(OP1), .OP0(OP0), .Cin(ula1_1bit_3_overflow));
endmodule

module ULA1_16Bits (
  input  InvB,
  input  Cin,
  input  [1:0] OP,
  input  [15:0] A,
  input  [15:0] B,
  output [15:0] S,
  output Overflow
);

  wire ula1_4bits_1_overflow, ula1_4bits_2_overflow, ula1_4bits_3_overflow;

  ULA1_4Bits ula1_4bits_1 (
    .Cin(Cin), .InvB(InvB), .A0(A[0]), .B0(B[0]), .A1(A[1]), .B1(B[1]), .A2(A[2]), .B2(B[2]), .A3(A[3]),
    .B3(B[3]), .s0(S[0]), .s1(S[1]), .s2(S[2]), .s3(S[3]), .OP1(OP[1]), .OP0(OP[0]),
    .Overflow(ula1_4bits_1_overflow));
  ULA1_4Bits ula1_4bits_2 (
    .Cin(ula1_4bits_1_overflow), .InvB(InvB), .A0(A[4]), .B0(B[4]), .A1(A[5]), .B1(B[5]), .A2(A[6]),
    .B2(B[6]), .A3(A[7]), .B3(B[7]), .s0(S[4]), .s1(S[5]), .s2(S[6]), .s3(S[7]), .OP1(OP[1]), .OP0(OP[0]),
    .Overflow(ula1_4bits_2_overflow));
  ULA1_4Bits ula1_4bits_3 (
    .Cin(ula1_4bits_2_overflow), .InvB(InvB), .A0(A[8]), .B0(B[8]), .A1(A[9]), .B1(B[9]), .A2(A[10]),
    .B2(B[10]), .A3(A[11]), .B3(B[11]), .s0(S[8]), .s1(S[9]), .s2(S[10]), .s3(S[11]), .OP1(OP[1]),
    .OP0(OP[0]), .Overflow(ula1_4bits_3_overflow));
  ULA1_4Bits ula1_4bits_4 (
    .Cin(ula1_4bits_3_overflow), .InvB(InvB), .A0(A[12]), .B0(B[12]), .A1(A[13]), .B1(B[13]), .A2(A[14]),
    .B2(B[14]), .A3(A[15]), .B3(B[15]), .s0(S[12]), .s1(S[13]), .s2(S[14]), .s3(S[15]), .OP1(OP[1]),
    .OP0(OP[0]), .Overflow(Overflow));
endmodule

module ULA2_1Bit (
  input  [3:0] A,
  input  [3:0] B,
  input  [3:0] OP,
  output [3:0] s
);

  wire [3:0] and_1_out, and_2_out, and_3_out, nand_1_out, nor_1_out, not_1_out, not_2_out, not_3_out,
       not_4_out, not_5_out, not_6_out, or_1_out, or_2_out, or_3_out, xnor_1_out, xor_1_out;

  assign not_1_out = ~A;  // NOT_Gate not_1, 4 bits wide
  assign nor_1_out = ~(A | B);  // NOR_Gate nor_1, 4 bits wide
  assign and_1_out = not_1_out & B;  // AND_Gate and_1, 4 bits wide
  assign nand_1_out = ~(A & B);  // NAND_Gate nand_1, 4 bits wide
  assign xor_1_out = A ^ B;  // XOR_Gate xor_1, 4 bits wide
  assign and_2_out = A & not_2_out;  // AND_Gate and_2, 4 bits wide
  assign not_2_out = ~B;  // NOT_Gate not_2, 4 bits wide
  assign not_3_out = ~A;  // NOT_Gate not_3, 4 bits wide
  assign or_1_out = not_3_out | B;  // OR_Gate or_1, 4 bits wide
  assign not_4_out = ~B;  // NOT_Gate not_4, 4 bits wide
  assign xnor_1_out = ~(A ^ B);  // XNOR_Gate xnor_1, 4 bits wide
  assign and_3_out = A & B;  // AND_Gate and_3, 4 bits wide
  assign or_2_out = A | not_4_out;  // OR_Gate or_2, 4 bits wide
  assign or_3_out = A | B;  // OR_Gate or_3, 4 bits wide
  assign not_5_out = ~A;  // NOT_Gate not_5, 4 bits wide
  assign not_6_out = ~B;  // NOT_Gate not_6, 4 bits wide
  Multiplexer #(.select(4), .width(4), .enable("false")) multiplexer_1 (
    .in0(not_5_out), .in1(nor_1_out), .in2(and_1_out), .in3(4'b0000), .in4(nand_1_out), .in5(not_6_out),
    .in6(xor_1_out), .in7(and_2_out), .in8(or_1_out), .in9(xnor_1_out), .in10(B), .in11(and_3_out),
    .in12(4'b1111), .in13(or_2_out), .in14(or_3_out), .in15(A), .out(s), .sel(OP));
endmodule

module main (
  input  [3:0] A,
  input  [3:0] B,
  input  [3:0] OP,
  output [3:0] S
);

  ULA2_1Bit ula2_1bit_1 (.A(A), .B(B), .s(S), .OP(OP));
endmodule
